# Fritzing sketch fairy_house_lights_diagram (saved by Fritzing 1.0.2b)
breadboards: 1

parts:
  Part3 = Arduino Uno (Rev3)
  M1 = IR break beam 3mm tx [package=THT]
  M2 = IR break beam 3mm rx [package=THT]
  NEOPIXEL1 = Neopixel Strip -- Black (30/m) [part_number=1376]

nets:
  N1: Part3.D4, M2.pin2
  N2: Part3.D6_PWM, NEOPIXEL1.Dout
  5V: Part3.5V, M1.pin1, M2.pin1, NEOPIXEL1.+5V
  GND: Part3.GND, M1.pin2, M2.pin3, NEOPIXEL1.GND

notes:
  Break-beam sensor
  neopixels

custom parts:
  IR break beam 3mm tx: Infrared break beam Sensor tx module.
  IR break beam 3mm rx: Infrared break beam Sensor rx module.
  Neopixel Strip -- Black (30/m): These NeoPixel strips have 30 digitally-addressable pixel LEDs per meter and are very affordable and are only 12.5 mm wide, 10 mm if you remove the strip from the casing.
