# Fritzing sketch ModulesMiniGolf_BreadboardDiagram (saved by Fritzing 1.0.2b)
breadboards: 1

parts:
  S1 = Tilt Switch [package=THT]
  A1 = DFPlayer Pro-a mini
  SP1 = SPEAKER [package=pcb_mount_speaker]
  SP2 = SPEAKER [package=pcb_mount_speaker]
  Part3 = Arduino Uno (Rev3)
  M1 = IR break beam 3mm tx [package=THT]
  M2 = IR break beam 3mm rx [package=THT]
  J1 = Basic Servo

nets:
  N1: S1.Pin_1, Part3.D8
  GND: S1.Pin_2, A1.Pin_2, Part3.GND, M1.pin2, M2.pin3, J1.gnd
  5V: A1.Pin_1, Part3.5V, M1.pin1, M2.pin1, J1.vcc
  N2: A1.Pin_3, Part3.D3_PWM
  N3: A1.Pin_4, Part3.D2
  N4: A1.Pin_7, SP2.-
  N5: A1.Pin_8, SP2.+
  N6: A1.Pin_9, SP1.-
  N7: A1.Pin_10, SP1.+
  N8: Part3.D9_PWM, J1.pulse
  N9: Part3.D7, M2.pin2

notes:
  Fast vibration sensor
  Break-beam sensor
  MP3 Player
  Servo

custom parts:
  DFPlayer Pro-a mini: DFPlayer Pro-a mini simple but powerful MP3 Player.
  IR break beam 3mm tx: Infrared break beam Sensor tx module.
  IR break beam 3mm rx: Infrared break beam Sensor rx module.
